# Fritzing sketch Schaltplan (saved by Fritzing 1.0.6)
breadboards: 1

parts:
  A1 = lilygo t-display-S3
  GC9A1 = GC9A01 1.28 inch Round TFT LCD-Display 240x240 [part_number=GC9A01]
  GC9A2 = GC9A01 1.28 inch Round TFT LCD-Display 240x240 [part_number=GC9A01]
  Raspberry_Pi_1 = Raspberry Pi 3 [part_number=RPI-3-V1.2]
  HC-SR04_Sensor_1 = HC-SR04 Ultrasonic Distance Sensor
  R2 = Resistor [tolerance=±5% power=0.25W resistance=2.2k package=THT]
  RGB_LED1 = RGB LED

nets:
  GND: A1.Pin_1, A1.Pin_2, A1.Pin_10, A1.Pin_11, A1.Pin_16, A1.Pin_18, GC9A1.GND, GC9A2.GND, Raspberry_Pi_1.GND, HC-SR04_Sensor_1.GND
  N1: A1.Pin_3, A1.Pin_14, Raspberry_Pi_1.GPIO15
  N2: A1.Pin_4, A1.Pin_13, Raspberry_Pi_1.GPIO14
  N3: A1.Pin_5, GC9A1.SCL, GC9A2.SCL
  N4: A1.Pin_6, GC9A1.SDA, GC9A2.SDA
  N5: A1.Pin_7, GC9A1.RST, GC9A2.RST
  N6: A1.Pin_8, GC9A1.DC, GC9A2.DC
  VCC: A1.Pin_12, A1.Pin_28, GC9A1.VCC, GC9A2.VCC
  5V: A1.Pin_17, Raspberry_Pi_1.5V, HC-SR04_Sensor_1.VCC
  N7: A1.Pin_24, GC9A1.CS, GC9A2.CS
  3V3: Raspberry_Pi_1.3v3, Raspberry_Pi_1.3V3, RGB_LED1.pin4
  N8: Raspberry_Pi_1.GPIO17, RGB_LED1.pin1
  N9: Raspberry_Pi_1.GPIO27, RGB_LED1.pin2
  N10: Raspberry_Pi_1.GPIO22, RGB_LED1.pin3
  N11: Raspberry_Pi_1.GPIO24, R2.Pin_0
  N12: Raspberry_Pi_1.GPIO23, HC-SR04_Sensor_1.TRIG
  N13: HC-SR04_Sensor_1.ECHO, R2.Pin_1

custom parts:
  lilygo t-display-S3: T-Display-S3 ESP32-S3 1.9 inch ST7789 LCD Display Development Board WIFI Bluetooth5.0 Wireless Module 170*320 Resolution.
  GC9A01 1.28 inch Round TFT LCD-Display 240x240: This is the front layout of a GC9A01 1,28inch Round TFT LCD-Display 240x240
